# Fritzing sketch 868 Arduino Nano PCB (saved by Fritzing 0.9.3b)
circuit board: 8.46667cm x 5.64444cm
perfboards: 1

parts:
  J1 = female pin header, 2 pins [form="♀ (female)"]
  R9 = Resistor [tolerance=±5% resistance=1.2k package=THT]
  R8 = Resistor [tolerance=±5% resistance=1.2k package=THT]
  R3 = Resistor [tolerance=±5% resistance=1.2k package=THT]
  J4 = female pin header, 2 pins [form="♀ (female)"]
  R4 = Resistor [tolerance=±5% resistance=1.2k package=THT]
  J3 = female pin header, 2 pins [form="♀ (female)"]
  R5 = Resistor [tolerance=±5% resistance=1.2k package=THT]
  R7 = Resistor [tolerance=±5% resistance=1.2k package=THT]
  R1 = Resistor [tolerance=±5% resistance=1.2k package=THT]
  J2 = female pin header, 2 pins [form="♀ (female)"]
  R6 = Resistor [tolerance=±5% resistance=1.2k package=THT]
  Part1 = Arduino Nano (Rev3.0)
  R2 = Resistor [tolerance=±5% resistance=1.2k package=THT]

nets:
  N1: J1.pin1, Part1.3V3
  N2: J1.pin2, R9.Pin_0, R1.Pin_0, R6.Pin_0, Part1.GND
  N3: R9.Pin_1, R7.Pin_0
  N4: R8.Pin_0, R7.Pin_1, J2.pin1
  N5: R8.Pin_1, Part1.D11/MOSI
  N6: R3.Pin_0, R1.Pin_1
  N7: R3.Pin_1, J4.pin2, R2.Pin_0
  N8: J4.pin1, Part1.D2
  N9: R4.Pin_0, R5.Pin_1, J2.pin2
  N10: R4.Pin_1, Part1.D13/SCK
  N11: J3.pin1, Part1.D12/MISO
  N12: R5.Pin_0, R6.Pin_1
  N13: Part1.D10, R2.Pin_1
